# Fritzing sketch circuit diagram (saved by Fritzing 0.9.5d)
breadboards: 1

parts:
  HC-SR04_Sensor_1 = HC-SR04 Ultrasonic Distance Sensor
  Part2 = Bluetooth HC-05 Macho
  M1 = fc-51 [package=THT]
  J2 = Basic Servo
  M2 = DC Motor
  L298N1 = L298N DC motor driver
  BAT1 = BC9VPC [package=bc9vpc]
  M3 = DC Motor
  J3 = Piezo Speaker
  Part1 = Arduino Uno (Rev3)

nets:
  VCC: HC-SR04_Sensor_1.VCC, Part2.VCC, M1.pin3, J2.vcc, Part1.5V
  N1: HC-SR04_Sensor_1.TRIG, Part1.A1
  N2: HC-SR04_Sensor_1.ECHO, Part1.A0
  GND: HC-SR04_Sensor_1.GND, Part2.GND, M1.pin2, J2.gnd, L298N1.GND, BAT1.V-, J3.pin1, Part1.GND
  N3: Part2.TXD, Part1.D2
  N4: Part2.RXD, Part1.D4
  N5: M1.pin1, Part1.D7
  N6: J2.pulse, Part1.D3_PWM
  N7: M2.pin_1, L298N1.OUT4
  N8: M2.pin_2, L298N1.OUT3
  N9: L298N1.OUT1, M3.pin_2
  N10: L298N1.OUT2, M3.pin_1
  N11: L298N1.12V, BAT1.V+
  5V: L298N1.5V, Part1.VIN
  N12: L298N1.ENA, Part1.D5_PWM
  N13: L298N1.ENB, Part1.D6_PWM
  N14: L298N1.IN1, Part1.D8
  N15: L298N1.IN2, Part1.D9_PWM
  N16: L298N1.IN3, Part1.D10_PWM/SS
  N17: L298N1.IN4, Part1.D11_PWM/MOSI
  N18: J3.pin2, Part1.D12/MISO

notes:
  LEFT MOTOR
  RIGHT MOTOR

custom parts:
  L298N DC motor driver: 2x DC motor driver with 78M05 positive voltage regulator (7..35 V) L298N: max 46 V, 2 A Set 5 V Enable jumper to enable 5 V regultor (needed for the L298N) and +5 V output at screw terminal or supply external +5 V at screw terminal Set ENA and/or ENB to +5 V to enable motor permanently or supply ENA and/or ENB with PWM signal IN1 and IN2 set rotation directory for motor A (OUT1/OUT2) IN2 and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

// code stored in the sketch: circuit diagram 2.ino
#include <Servo.h>
#include <SoftwareSerial.h>

SoftwareSerial BT(2, 4);   // HC-05 TX->D2 RX->D4
Servo myservo;

// Ultrasonic
#define trigPin A1
#define echoPin A0

// Rear IR
#define rearIR 7

// Buzzer
#define BUZZER 12

// L298N
#define ENA 5
#define ENB 6

#define IN1 8
#define IN2 9
#define IN3 10
#define IN4 11

String currentCommand = "stop";

void setup()
{
  Serial.begin(9600);
  BT.begin(9600);

  pinMode(trigPin, OUTPUT);
  pinMode(echoPin, INPUT);

  pinMode(rearIR, INPUT);

  pinMode(BUZZER, OUTPUT);

  pinMode(ENA, OUTPUT);
  pinMode(ENB, OUTPUT);

  pinMode(IN1, OUTPUT);
  pinMode(IN2, OUTPUT);
  pinMode(IN3, OUTPUT);
  pinMode(IN4, OUTPUT);

  analogWrite(ENA, 180);
  analogWrite(ENB, 180);

  myservo.attach(3);
  myservo.write(90);

  stopRobot();

  Serial.println("Robot Ready");
}

void loop()
{
  // Continuous rear obstacle protection
  if(currentCommand == "backward" && digitalRead(rearIR) == 0)
  {
    stopRobot();
    currentCommand = "stop";
    longBeep();
    Serial.println("Rear Obstacle");
  }

  // Continuous front obstacle protection
  if(currentCommand == "forward" && frontDistance() < 20)
  {
    stopRobot();
    currentCommand = "stop";
    beep();
    Serial.println("Front Obstacle");
  }

  if(BT.available())
  {
    String cmd = BT.readStringUntil('\n');

    cmd.trim();
    cmd.toLowerCase();

    Serial.print("Received: ");
    Serial.println(cmd);

    if(cmd == "forward")
    {
      if(frontDistance() > 25)
      {
        forward();
        currentCommand = "forward";
      }
      else
      {
        stopRobot();
        beep();
      }
    }

    else if(cmd == "backward")
    {
      if(digitalRead(rearIR) == 1)
      {
        backward();
        currentCommand = "backward";
      }
      else
      {
        stopRobot();
        longBeep();
      }
    }

    else if(cmd == "left")
    {
      myservo.write(160);
      delay(400);

      if(frontDistance() > 25)
      {
        leftTurn();
        currentCommand = "left";
      }
      else
      {
        stopRobot();
        beep();
      }

      myservo.write(90);
    }

    else if(cmd == "right")
    {
      myservo.write(20);
      delay(400);

      if(frontDistance() > 25)
      {
        rightTurn();
        currentCommand = "right";
      }
      else
      {
        stopRobot();
        beep();
      }

      myservo.write(90);
    }

    else if(cmd == "stop")
    {
      stopRobot();
      currentCommand = "stop";
    }
  }
}

// =====================
// DISTANCE FUNCTION
// =====================

int frontDistance()
{
  digitalWrite(trigPin, LOW);
  delayMicroseconds(2);

  digitalWrite(trigPin, HIGH);
  delayMicroseconds(10);

  digitalWrite(trigPin, LOW);

  long duration = pulseIn(echoPin, HIGH, 30000);

  if(duration == 0)
    return 300;

  return duration * 0.034 / 2;
}

// =====================
// BUZZER
// =====================


void beep()
{
  digitalWrite(BUZZER, HIGH);
  delay(100);
  digitalWrite(BUZZER, LOW);
}

void longBeep()
{
  digitalWrite(BUZZER, HIGH);
  delay(500);
  digitalWrite(BUZZER, LOW);
}

// =====================
// MOTOR FUNCTIONS
// =====================

void forward()
{
  digitalWrite(IN1, LOW);
  digitalWrite(IN2, HIGH);

  digitalWrite(IN3, LOW);
  digitalWrite(IN4, HIGH);
}

void backward()
{
  digitalWrite(IN1, HIGH);
  digitalWrite(IN2, LOW);

  digitalWrite(IN3, HIGH);
  digitalWrite(IN4, LOW);
}

void leftTurn()
{
  digitalWrite(IN1, HIGH);
  digitalWrite(IN2, LOW);

  digitalWrite(IN3, LOW);
  digitalWrite(IN4, HIGH);
}

void rightTurn()
{
  digitalWrite(IN1, LOW);
  digitalWrite(IN2, HIGH);

  digitalWrite(IN3, HIGH);
  digitalWrite(IN4, LOW);
}

void stopRobot()
{
  digitalWrite(IN1, LOW);
  digitalWrite(IN2, LOW);

  digitalWrite(IN3, LOW);
  digitalWrite(IN4, LOW);
}
